# Fritzing sketch bird (saved by Fritzing 0.9.4)
circuit board: 8.46667cm x 5.64444cm

parts:
  SP1 = SPEAKER [package=pcb_mount_speaker]  # not connected
  Mod1 = TP4056 [part_number=TP4056]
  Bat1 = battery_holder_dual_18650 [part_number=TBH-18650-2A-P]
  Componente3 = Solar Cell
  M2 = DOIT Esp32 DevKit v1 (30 pins long, 11 pins width) [part_number=ESP32S-PIN30]
  Componente4 = Solar Cell
  M3 = DC Motor
  Part2 = SparkFun Motor Driver TB6612FNG (v11) [part_number=ROB-14451]
  Part1 = Adafruit MAX98357A I2S 3W Class D Amplifier [part_number="Adafruit #3006"]
  M1 = MT3608 Module

nets:
  N1: Mod1.pin1, Componente3.+, Componente4.+
  N2: Mod1.pin2, Componente3.-, Componente4.-
  N3: Mod1.pin4, Bat1.+#2, Bat1.+#3, M1.pin2
  N4: Mod1.pin5, Bat1.+#0, Bat1.+#1, M1.pin1
  3V3: M2.3V3, Part2.VCC, Part1.VIN
  GND: M2.GND, Part1.GND, M1.pin4
  N5: M2.D33, Part1.DIN
  N6: M2.D25, Part1.BCLK
  N7: M2.D26, Part1.LRCLK
  N8: M2.D27, Part2.PWMA
  N9: M2.D14, Part2.AIN2
  N10: M2.D12, Part2.AIN1
  N11: M2.D13, Part2.STBY
  N12: M2.VIN, Part2.VM, M1.pin3
  N13: M3.pin_1, Part2.A02
  N14: M3.pin_2, Part2.A01

custom parts:
  TP4056: TP4056 Lithium battery charger / protection module. (this one has the pins on .1 boundaried unlike the original)
  battery_holder_dual_18650: TBH-18650-2A-P dual 18650 battery holder.
  DOIT Esp32 DevKit v1 (30 pins long, 11 pins width): The DOIT Esp32 DevKit v1 is one of the development board created by DOIT to evaluate the ESP-WROOM-32 module. It is based on the ESP32 microcontroller that boasts Wifi, Bluetooth, Ethernet and Low Power support all in a single chip. (vanepp) made breadboard work, adjusted pin numbering and labels and reduced size of schematic and cleaned up pcb. This chip is 30pins long (2 x15) and 11 pins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
  SparkFun Motor Driver TB6612FNG (v11): The TB6612FNG Motor Driver can control up to two DC motors at a constant current of 1.2A (3.2A peak). Two input signals (IN1 and IN2) can be used to control the motor in one of four function modes: CW, CCW, short-brake and stop. The two motor outputs (A and B) can be separately controlled, and the speed of each motor is controlled via a PWM input signal with a frequency up to 100kHz. The STBY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
  Adafruit MAX98357A I2S 3W Class D Amplifier: Listen to this good news - we now have an all in one digital audio amp breakout board that works incredibly well with the Raspberry Pi! If you're looking for an easy and low cost way to get you digital sound files bumpin' then the MAX08357 I2S Amp Breakout is for you. It takes standard I2S digital audio input and, not only decodes it into analog, but also amplifies it directly into a speaker.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
  MT3608 Module: MT3608 Boost Converter Module Links: Aerosemi MT3608 2A Step Up Converter datasheet

// code stored in the sketch: Untitled2.ino

// i2s pins
i2s_pin_config_t i2sPins = {
    .bck_io_num = 25,//this is BCK pin
    .ws_io_num = 26,// this is LRCK pin
    .data_out_num = 33,// this is DATA output pin
    .data_in_num = -1
};



const int pinPWMA = 27;
const int pinAIN2 = 14;
const int pinAIN1 = 12;
const int pinSTBY = 13;
