# Fritzing sketch bird1 (saved by Fritzing 0.9.4)
circuit board: 6.01232cm x 3.87188cm
circuit board: 8.18384cm x 2.83452cm

parts:
  SP1 = SPEAKER [package=pcb_mount_speaker]
  Bat1 = battery_holder_dual_18650 [part_number=TBH-18650-2A-P]
  Componente3 = Solar Cell
  M2 = DOIT Esp32 DevKit v1 (30 pins long, 11 pins width) [part_number=ESP32S-PIN30]
  Componente4 = Solar Cell
  M3 = DC Motor
  Part2 = SparkFun Motor Driver TB6612FNG (v11) [part_number=ROB-14451]
  Part1 = Adafruit MAX98357A I2S 3W Class D Amplifier [part_number="Adafruit #3006"]
  M1 = MT3608 Module
  J1 = female pin header, 2 pins [form="♀ (female)"]
  J2 = female pin header, 2 pins [form="♀ (female)"]
  R1 = Resistor [tolerance=±5% resistance=100k package=THT]
  R2 = Resistor [tolerance=±5% resistance=390k package=THT]
  R3 = Resistor [tolerance=±5% resistance=330k package=THT]
  J3 = female pin header, 2 pins [form="♀ (female)"]
  Mod1 = TP4056 [part_number=TP4056]

nets:
  N1: SP1.+, Part1.VO-, J1.pin2
  N2: SP1.-, Part1.VO+, J1.pin1
  N3: Bat1.+#0, Bat1.+#1, M1.pin1, Mod1.pin5
  N4: Bat1.+#2, Bat1.+#3, M1.pin2, Mod1.pin4
  N5: Componente3.+, Componente4.+, R2.Pin_0, J3.pin1, Mod1.pin1
  N6: Componente3.-, Componente4.-, Mod1.pin2
  3V3: M2.3V3, Part2.VCC, Part1.VIN
  GND: M2.GND, Part2.GND, Part1.GND, M1.pin4, J2.pin2, R1.Pin_1, R3.Pin_1
  N7: M2.D32, R2.Pin_1, R3.Pin_0
  N8: M2.D33, Part1.LRCLK
  N9: M2.D25, Part1.BCLK
  N10: M2.D26, Part1.DIN
  N11: M2.D27, Part2.STBY
  N12: M2.D14, Part2.AIN1
  N13: M2.D12, Part2.AIN2
  N14: M2.D13, Part2.PWMA
  N15: M2.VIN, Part2.VM, M1.pin3, J2.pin1
  N16: M3.pin_1, Part2.A02
  N17: M3.pin_2, Part2.A01
  N18: Part1.GAIN, R1.Pin_0

custom parts:
  battery_holder_dual_18650: TBH-18650-2A-P dual 18650 battery holder.
  DOIT Esp32 DevKit v1 (30 pins long, 11 pins width): The DOIT Esp32 DevKit v1 is one of the development board created by DOIT to evaluate the ESP-WROOM-32 module. It is based on the ESP32 microcontroller that boasts Wifi, Bluetooth, Ethernet and Low Power support all in a single chip. (vanepp) made breadboard work, adjusted pin numbering and labels and reduced size of schematic and cleaned up pcb. This chip is 30pins long (2 x15) and 11 pins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
  SparkFun Motor Driver TB6612FNG (v11): The TB6612FNG Motor Driver can control up to two DC motors at a constant current of 1.2A (3.2A peak). Two input signals (IN1 and IN2) can be used to control the motor in one of four function modes: CW, CCW, short-brake and stop. The two motor outputs (A and B) can be separately controlled, and the speed of each motor is controlled via a PWM input signal with a frequency up to 100kHz. The STBY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
  Adafruit MAX98357A I2S 3W Class D Amplifier: Listen to this good news - we now have an all in one digital audio amp breakout board that works incredibly well with the Raspberry Pi! If you're looking for an easy and low cost way to get you digital sound files bumpin' then the MAX08357 I2S Amp Breakout is for you. It takes standard I2S digital audio input and, not only decodes it into analog, but also amplifies it directly into a speaker.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
  MT3608 Module: MT3608 Boost Converter Module Links: Aerosemi MT3608 2A Step Up Converter datasheet
  TP4056: TP4056 Lithium battery charger / protection module. (this one has the pins on .1 boundaried unlike the original)

// code stored in the sketch: Untitled2.ino
vout = Vin * r2)
